# Fritzing sketch wiring-schema (saved by Fritzing 1.0.6)

parts:
  Pro_Micro1 = Pro Micro
  S1 = Square Pushbutton
  S2 = Square Pushbutton
  S3 = Square Pushbutton
  S4 = Square Pushbutton
  S5 = Square Pushbutton
  S6 = Square Pushbutton
  S7 = Square Pushbutton
  S8 = Square Pushbutton
  S9 = Square Pushbutton
  SSD1306_OLED_Display_0_96_inch_128x64 = SSD1306 0.96in 128x64 I2C Monochrome OLED Display
  ENCODER1 = Rotary Encoder with switch (KY-040) [part_number=KY-040]

nets:
  N1: Pro_Micro1.D2, SSD1306_OLED_Display_0_96_inch_128x64.SDA
  N2: Pro_Micro1.D3, SSD1306_OLED_Display_0_96_inch_128x64.SCL
  N3: Pro_Micro1.D4, S1.leg1
  N4: Pro_Micro1.D5, S2.leg1
  N5: Pro_Micro1.D6, S3.leg1
  N6: Pro_Micro1.D7, S4.leg1
  N7: Pro_Micro1.D8, S5.leg1
  N8: Pro_Micro1.D9, S6.leg1
  N9: Pro_Micro1.D10, S4.leg0, S5.leg0, S6.leg0, ENCODER1.GND, ENCODER1.+
  N10: Pro_Micro1.D16/MOSI, ENCODER1.DT
  N11: Pro_Micro1.D14/MISO, ENCODER1.SW
  N12: Pro_Micro1.D15/SCLK, S7.leg1
  N13: Pro_Micro1.D18/A0, S8.leg1
  N14: Pro_Micro1.D19/A1, S9.leg1
  VCC: Pro_Micro1.VCC, SSD1306_OLED_Display_0_96_inch_128x64.VCC
  GND: Pro_Micro1.GND, S7.leg0, S8.leg0, S9.leg0, SSD1306_OLED_Display_0_96_inch_128x64.GND, ENCODER1.CLK
  N15: S1.leg0, S2.leg0, S3.leg0

custom parts:
  Pro Micro: The SparkFun Pro Micro is a complete USB-based microcontoller development system, in a very small footprint, capable of implementing many types of projects. All programming can be done via the USB port.
  Rotary Encoder with switch (KY-040): A Rotary Encoder with switch

// code stored in the sketch: Untitled2.ino
#include <Keypad.h>

const byte ROWS = 3; 
const byte COLS = 3; 

// Definisci la mappa fisica dei tasti
char hexaKeys[ROWS][COLS] = {
  {'1','2','3'},
  {'4','5','6'},
  {'7','8','9'}
};

byte rowPins[ROWS] = {4, 5, 6}; // Pin collegati alle righe
byte colPins[COLS] = {7, 8, 9}; // Pin collegati alle colonne

Keypad customKeypad = Keypad(makeKeymap(hexaKeys), rowPins, colPins, ROWS, COLS); 

void loop(){
  char customKey = customKeypad.getKey();
  
  if (customKey){
    // Se customKey è '1', fai CTRL+C, ecc...
  }
}
